// Digital circuit 1X15_SRAM.dig as structural Verilog
module _1X15_SRAM (
  input  WS,
  input  RS1,
  input  RS2,
  input  [14:0] WD_14_0,
  input  CLK,
  output [14:0] RD1_14_0,
  output [14:0] RD2_14_0
);

  _1into1_SRAM _1into1_sram_1 (
    .WD(WD_14_0[14]), .WS(WS), .RS1(RS1), .RS2(RS2), .CLK(CLK), .RD1(RD1_14_0[14]), .RD2(RD2_14_0[14]));
  _1into1_SRAM _1into1_sram_2 (
    .WD(WD_14_0[11]), .WS(WS), .RS1(RS1), .RS2(RS2), .CLK(CLK), .RD1(RD1_14_0[11]), .RD2(RD2_14_0[11]));
  _1into1_SRAM _1into1_sram_3 (
    .WD(WD_14_0[8]), .WS(WS), .RS1(RS1), .RS2(RS2), .CLK(CLK), .RD1(RD1_14_0[8]), .RD2(RD2_14_0[8]));
  _1into1_SRAM _1into1_sram_4 (
    .WD(WD_14_0[5]), .WS(WS), .RS1(RS1), .RS2(RS2), .CLK(CLK), .RD1(RD1_14_0[5]), .RD2(RD2_14_0[5]));
  _1into1_SRAM _1into1_sram_5 (
    .WD(WD_14_0[2]), .WS(WS), .RS1(RS1), .RS2(RS2), .CLK(CLK), .RD1(RD1_14_0[2]), .RD2(RD2_14_0[2]));
  _1into1_SRAM _1into1_sram_6 (
    .WD(WD_14_0[13]), .WS(WS), .RS1(RS1), .RS2(RS2), .CLK(CLK), .RD1(RD1_14_0[13]), .RD2(RD2_14_0[13]));
  _1into1_SRAM _1into1_sram_7 (
    .WD(WD_14_0[10]), .WS(WS), .RS1(RS1), .RS2(RS2), .CLK(CLK), .RD1(RD1_14_0[10]), .RD2(RD2_14_0[10]));
  _1into1_SRAM _1into1_sram_8 (
    .WD(WD_14_0[7]), .WS(WS), .RS1(RS1), .RS2(RS2), .CLK(CLK), .RD1(RD1_14_0[7]), .RD2(RD2_14_0[7]));
  _1into1_SRAM _1into1_sram_9 (
    .WD(WD_14_0[4]), .WS(WS), .RS1(RS1), .RS2(RS2), .CLK(CLK), .RD1(RD1_14_0[4]), .RD2(RD2_14_0[4]));
  _1into1_SRAM _1into1_sram_10 (
    .WD(WD_14_0[1]), .WS(WS), .RS1(RS1), .RS2(RS2), .CLK(CLK), .RD1(RD1_14_0[1]), .RD2(RD2_14_0[1]));
  _1into1_SRAM _1into1_sram_11 (
    .WD(WD_14_0[12]), .WS(WS), .RS1(RS1), .RS2(RS2), .CLK(CLK), .RD1(RD1_14_0[12]), .RD2(RD2_14_0[12]));
  _1into1_SRAM _1into1_sram_12 (
    .WD(WD_14_0[9]), .WS(WS), .RS1(RS1), .RS2(RS2), .CLK(CLK), .RD1(RD1_14_0[9]), .RD2(RD2_14_0[9]));
  _1into1_SRAM _1into1_sram_13 (
    .WD(WD_14_0[6]), .WS(WS), .RS1(RS1), .RS2(CLK), .CLK(RS2), .RD1(RD1_14_0[6]), .RD2(RD2_14_0[6]));
  _1into1_SRAM _1into1_sram_14 (
    .WD(WD_14_0[3]), .WS(WS), .RS1(RS1), .RS2(RS2), .CLK(CLK), .RD1(RD1_14_0[3]), .RD2(RD2_14_0[3]));
  _1into1_SRAM _1into1_sram_15 (
    .WD(WD_14_0[0]), .WS(WS), .RS1(RS1), .RS2(RS2), .CLK(CLK), .RD1(RD1_14_0[0]), .RD2(RD2_14_0[0]));

  // Other names for the same wires on the sheet: RD1_0 = RD1_14_0[0]; RD1_1 = RD1_14_0[1]; RD1_2 = RD1_14_0[2];
  //   RD1_3 = RD1_14_0[3]; RD1_4 = RD1_14_0[4]; RD1_5 = RD1_14_0[5]; RD1_6 = RD1_14_0[6]; RD1_7 = RD1_14_0[7];
  //   RD1_8 = RD1_14_0[8]; RD1_9 = RD1_14_0[9]; RD1_10 = RD1_14_0[10]; RD1_11 = RD1_14_0[11]; RD1_12 = RD1_14_0[12];
  //   RD1_13 = RD1_14_0[13]; RD1_14 = RD1_14_0[14]; RD2_0 = RD2_14_0[0]; RD2_1 = RD2_14_0[1]; RD2_2 = RD2_14_0[2];
  //   RD2_3 = RD2_14_0[3]; RD2_4 = RD2_14_0[4]; RD2_5 = RD2_14_0[5]; RD2_6 = RD2_14_0[6]; RD2_7 = RD2_14_0[7];
  //   RD2_8 = RD2_14_0[8]; RD2_9 = RD2_14_0[9]; RD2_10 = RD2_14_0[10]; RD2_11 = RD2_14_0[11]; RD2_12 = RD2_14_0[12];
  //   RD2_13 = RD2_14_0[13]; RD2_14 = RD2_14_0[14]; WD0 = WD_14_0[0]; WD1 = WD_14_0[1]; WD2 = WD_14_0[2];
  //   WD3 = WD_14_0[3]; WD4 = WD_14_0[4]; WD5 = WD_14_0[5]; WD6 = WD_14_0[6]; WD7 = WD_14_0[7]; WD8 = WD_14_0[8];
  //   WD9 = WD_14_0[9]; WD10 = WD_14_0[10]; WD11 = WD_14_0[11]; WD12 = WD_14_0[12]; WD13 = WD_14_0[13];
  //   WD14 = WD_14_0[14]
endmodule
