// Digital circuit 3BIT Reg.dig as structural Verilog
module _3BIT_Reg (
  input  [2:0] Din_2_0,
  input  Sel,
  input  CLK,
  output [2:0] Dout_2_0
);

  _1bit_REG _1bit_reg_1 (.D_in(Din_2_0[2]), .Sel(Sel), .CLK(CLK), .D_out(Dout_2_0[2]));
  _1bit_REG _1bit_reg_2 (.D_in(Din_2_0[1]), .Sel(Sel), .CLK(CLK), .D_out(Dout_2_0[1]));
  _1bit_REG _1bit_reg_3 (.D_in(Din_2_0[0]), .Sel(Sel), .CLK(CLK), .D_out(Dout_2_0[0]));

  // Other names for the same wires on the sheet: B0 = Dout_2_0[0]; B1 = Dout_2_0[1]; B2 = Dout_2_0[2];
  //   A0 = Din_2_0[0]; A1 = Din_2_0[1]; A2 = Din_2_0[2]
endmodule
