// Digital circuit 3bit_PROG_COUNTER.dig as structural Verilog
module _3bit_PROG_COUNTER (
  input  [2:0] I_2_0,
  input  CLK,
  output [2:0] O_2_0
);

  _3BIT_Reg _3bit_reg_1 (.Din_2_0(I_2_0), .Sel(1'b1), .CLK(CLK), .Dout_2_0(O_2_0));
endmodule
