// Digital circuit 5bit_CU.dig as structural Verilog
module _5bit_CU (
  input  [3:0] OPCODE_3_0,
  input  [3:0] ZF,
  output [1:0] Op_1_0,
  output REG_EN,
  output IMM_SEL,
  output JMP_SEL
);

  wire and_1_out, and_3_out, and_4_out, and_5_out, or_1_out;

  and and_1 (and_1_out, ~OPCODE_3_0[2], ~OPCODE_3_0[3]);  // And
  and and_2 (IMM_SEL, OPCODE_3_0[2], ~OPCODE_3_0[3]);  // And
  and and_3 (and_3_out, ~OPCODE_3_0[2], OPCODE_3_0[3]);  // And
  and and_4 (and_4_out, ~OPCODE_3_0[0], ~OPCODE_3_0[1]);  // And
  and and_5 (and_5_out, OPCODE_3_0[0], ~OPCODE_3_0[1], ZF[0]);  // And
  or or_1 (or_1_out, and_4_out, and_5_out);
  or or_2 (REG_EN, and_1_out, IMM_SEL);
  and and_6 (JMP_SEL, and_3_out, or_1_out);
  // Pins of 1 and 4 bits meet at ZF

  assign Op_1_0 = OPCODE_3_0[1:0];
endmodule
