// Digital circuit 5bit_REG.dig as structural Verilog
module _5bit_REG (
  input  [4:0] A_4_0,
  input  Sel,
  input  CLK,
  output [4:0] R_4_0
);

  _1bit_REG _1bit_reg_1 (.D_in(A_4_0[4]), .Sel(Sel), .CLK(CLK), .D_out(R_4_0[4]));
  _1bit_REG _1bit_reg_2 (.D_in(A_4_0[3]), .Sel(Sel), .CLK(CLK), .D_out(R_4_0[3]));
  _1bit_REG _1bit_reg_3 (.D_in(A_4_0[2]), .Sel(Sel), .CLK(CLK), .D_out(R_4_0[2]));
  _1bit_REG _1bit_reg_4 (.D_in(A_4_0[1]), .Sel(Sel), .CLK(CLK), .D_out(R_4_0[1]));
  _1bit_REG _1bit_reg_5 (.D_in(A_4_0[0]), .Sel(Sel), .CLK(CLK), .D_out(R_4_0[0]));

  // Other names for the same wires on the sheet: A0 = A_4_0[0]; A1 = A_4_0[1]; A2 = A_4_0[2]; A3 = A_4_0[3];
  //   A4 = A_4_0[4]; B0 = R_4_0[0]; B1 = R_4_0[1]; B2 = R_4_0[2]; B3 = R_4_0[3]; B4 = R_4_0[4]
endmodule
