// Digital circuit 5bit_REG_SET.dig as structural Verilog
module _5bit_REG_SET (
  input  [1:0] WR_1_0,
  input  WE,
  input  [4:0] WRD_4_0,
  input  CLK,
  input  [1:0] RA_1_0,
  input  [1:0] RB_1_0,
  output [4:0] A_4_0,
  output [4:0] B_4_0
);

  wire A0, A1, A2, A3, D0, D1, D2, D3;
  wire [4:0] R0, R1, R2, R3;

  and and_1 (D3, A3, WE);
  and and_2 (D1, A1, WE);
  Decoder #(.Selector_Bits(2)) decoder_1 (.sel(WR_1_0), .out_0(A0), .out_1(A1), .out_2(A2), .out_3(A3));
  and and_3 (D2, A2, WE);
  and and_4 (D0, A0, WE);
  _5bit_REG _5bit_reg_1 (.A_4_0(WRD_4_0), .Sel(D3), .CLK(CLK), .R_4_0(R3));
  _5bit_REG _5bit_reg_2 (.A_4_0(WRD_4_0), .Sel(D2), .CLK(CLK), .R_4_0(R2));
  _5bit_REG _5bit_reg_3 (.A_4_0(WRD_4_0), .Sel(D1), .CLK(CLK), .R_4_0(R1));
  _5bit_REG _5bit_reg_4 (.A_4_0(WRD_4_0), .Sel(D0), .CLK(CLK), .R_4_0(R0));
  Multiplexer #(.Selector_Bits(2), .Bits(5)) multiplexer_1 (
    .sel(RA_1_0), .in_0(R0), .in_1(R1), .in_2(R2), .in_3(R3), .out(A_4_0));
  Multiplexer #(.Selector_Bits(2), .Bits(5)) multiplexer_2 (
    .sel(RB_1_0), .in_0(R0), .in_1(R1), .in_2(R2), .in_3(R3), .out(B_4_0));

  // Other names for the same wires on the sheet: WR[1:0] = WR_1_0; WRD[4:0] = WRD_4_0
endmodule
