// Digital circuit CPU.dig as structural Verilog
module CPU (
  input  [2:0] WR_2_0,
  input  WE,
  input  [14:0] WRD_14_0,
  input  CLK,
  input  PC_EN,
  input  [2:0] RA2_2_0,
  input  [3:0] ZF,
  output [14:0] RD2_14_0,
  output [4:0] R_4_0,
  output [1:0] R2_1_0,
  output [1:0] R1_1_0,
  output [1:0] WR_1_0,
  output [4:0] A_4_0,
  output [4:0] B_4_0,
  output [4:0] IMM_VAL_4_0
);

  wire CPU_CLK, IMM_SEL, JMP_SEL, REG_EN;
  wire [1:0] OP, XX;
  wire [2:0] _3bit_pc_adder_1_o_2_0, _3bit_prog_counter_1_o_2_0, multiplexer_1_out;
  wire [3:0] _7x15_sram_1_rd1_14_0;
  wire [4:0] _5bit_reg_set_1_b_4_0;

  Multiplexer #(.Bits(3)) multiplexer_1 (
    .sel(JMP_SEL), .in_0(_3bit_pc_adder_1_o_2_0), .in_1(IMM_VAL_4_0[4:2]), .out(multiplexer_1_out));
  _3bit_PROG_COUNTER _3bit_prog_counter_1 (
    .I_2_0(multiplexer_1_out), .CLK(CPU_CLK), .O_2_0(_3bit_prog_counter_1_o_2_0));
  _3bit_PC_ADDER _3bit_pc_adder_1 (.I_2_0(_3bit_prog_counter_1_o_2_0), .O_2_0(_3bit_pc_adder_1_o_2_0));
  and and_1 (CPU_CLK, PC_EN, CLK);
  _7X15_SRAM _7x15_sram_1 (
    .RA1_2_0(_3bit_prog_counter_1_o_2_0), .RA2_2_0(RA2_2_0), .WR_2_0(WR_2_0), .WRD_14_0(WRD_14_0), .WE(WE),
    .CLK(CLK), .RD1_14_0({_7x15_sram_1_rd1_14_0, R1_1_0, R2_1_0, IMM_VAL_4_0, XX}), .RD2_14_0(RD2_14_0));
  _5bit_CU _5bit_cu_1 (
    .OPCODE_3_0(_7x15_sram_1_rd1_14_0), .ZF(ZF), .Op_1_0(OP), .REG_EN(REG_EN), .IMM_SEL(IMM_SEL),
    .JMP_SEL(JMP_SEL));
  _5bit_REG_SET _5bit_reg_set_1 (
    .WR_1_0(R1_1_0), .CLK(CPU_CLK), .WE(REG_EN), .WRD_4_0(R_4_0), .A_4_0(A_4_0),
    .B_4_0(_5bit_reg_set_1_b_4_0), .RA_1_0(R1_1_0), .RB_1_0(R2_1_0));
  _5bit_ALU _5bit_alu_1 (.A_4_0(A_4_0), .B_4_0(B_4_0), .R_4_0(R_4_0), .OP_1_0(OP));
  Multiplexer #(.Bits(5)) multiplexer_2 (.sel(IMM_SEL), .in_0(_5bit_reg_set_1_b_4_0), .in_1(IMM_VAL_4_0), .out(B_4_0));
  // Pins of 1 and 4 bits meet at ZF

  assign WR_1_0 = R1_1_0;

  // Other names for the same wires on the sheet: XXXXX[4:0] = IMM_VAL_4_0; JMP_ADD[2:0] = IMM_VAL_4_0[4:2];
  //   R2[1:0] = R2_1_0; R1[1:0] = R1_1_0; A[4:0] = A_4_0; B[4:0] = B_4_0; R[4:0] = R_4_0; RA2[2:0] = RA2_2_0;
  //   RD2[14:0] = RD2_14_0; WR[2:0] = WR_2_0; WRD[14:0] = WRD_14_0

  // Notes on the sheet:
  //   Register Mode(00) = 2bit (type of operation) + 2bit(op) + 2bit(reg1) + 2bit(reg) + 7bit (don't Care)
  //   Immediate Mode(01) = 2bit (type of operation) + 2bit(op) + 2bit(reg1) + 5bit(value) + 4 bit(don't care)
  //   jump Mode(10) = 2bit (type of operation) + 2bit(op) + 4bit(add) + 7 bit(don't care)
  //   JMP(OP-00), JNC(OP-01)
  //   Op(00) = ADD
  //   Op(01) = ROL
  //   Op(10) = OR
  //   JE START -> 1001000100000
  //   START: OR R1,R1 -> 001001010000000
  //   JMP_TO: ADD R1,5 ->  010001010010100
  //   JMP JMP_TO -> 1000000100000
endmodule
